# Fritzing sketch Wortuhr (saved by Fritzing 0.9.3b)
circuit board: 5.71986cm x 4.60844cm
breadboards: 1

parts:
  Part1 = Adafruit Feather HUZZAH ESP8266 [part_number="Adafruit #2821"]
  R1 = Resistor [tolerance=±5% resistance=330 package=THT]
  C1 = Electrolytic Capacitor [capacitance=1000µF voltage=16V package="300 mil [THT, electrolytic]"]
  IC1 = IC, DIP package, 14 pins [chip_label=74AHCT125]
  J1 = screw terminal, 3 pins

nets:
  N1: Part1.GND, C1.-, IC1.pin1, IC1.pin7, J1.pin3
  N2: Part1.VBUS, C1.+, IC1.pin14, J1.pin1
  N3: Part1.GPIO15, IC1.pin2
  N4: R1.Pin_0, IC1.pin3
  N5: R1.Pin_1, J1.pin2

custom parts:
  Adafruit Feather HUZZAH ESP8266: his is the Adafruit Feather HUZZAH ESP8266 - our take on an 'all-in-one' ESP8266 WiFi development board with built in USB and battery charging. Its an ESP8266 WiFi module with all the extras you need, ready to rock! We have other boards in the Feather family, check'em out here. At the Feather HUZZAH's heart is an ESP8266 WiFi microcontroller clocked at 80 MHz and at 3.3V logic. This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
